# Fritzing sketch robo_sumo (saved by Fritzing 0.9.3b)
breadboards: 1

parts:
  MOTOR2 = 28BYJ-48 Stepper Motor
  MOTOR1 = 28BYJ-48 Stepper Motor
  Driver1 = 28BYJ-48 Driver Module [part_number=ULN2003 package=THT]
  Driver2 = 28BYJ-48 Driver Module [part_number=ULN2003 package=THT]
  VCC1 = Battery block 9V
  R2 = Photocell (LDR) [package=THT]
  R3 = Resistor [tolerance=±5% resistance=1k package="0402 [SMD]"]
  R4 = Resistor [tolerance=±5% resistance=1k package="0603 [SMD]"]
  R1 = Photocell (LDR) [package=THT]
  LED1 = smd LED [color="White (4500K)" package="1206 [SMD]"]
  LED2 = smd LED [color="White (4500K)" package="1206 [SMD]"]
  R5 = Resistor [tolerance=±5% resistance=220 package="2512 [SMD]"]
  R6 = Resistor [tolerance=±5% resistance=220 package="0805 [SMD]"]
  U1 = LuaNode32 / ESP32 [part_number=ESP32S-PIN30]
  LED3 = smd LED [color="Red (633nm)" package="1206 [SMD]"]
  LED4 = smd LED [color="Green (555nm)" package="1206 [SMD]"]
  R7 = Resistor [tolerance=±5% resistance=220 package="2512 [SMD]"]
  R8 = Resistor [tolerance=±5% resistance=220 package="2512 [SMD]"]
  LED5 = smd LED [color="Blue (430nm)" package="1206 [SMD]"]
  R9 = Resistor [tolerance=±5% resistance=220 package="2512 [SMD]"]

nets:
  N1: MOTOR2.RED, Driver2.red-pin
  N2: MOTOR2.ORANGE, Driver2.orange-pin
  N3: MOTOR2.YELLOW, Driver2.yellow-pin
  N4: MOTOR2.PINK, Driver2.pink-pin
  N5: MOTOR2.BLUE, Driver2.blue-pin
  N6: MOTOR1.RED, Driver1.red-pin
  N7: MOTOR1.ORANGE, Driver1.orange-pin
  N8: MOTOR1.YELLOW, Driver1.yellow-pin
  N9: MOTOR1.PINK, Driver1.pink-pin
  N10: MOTOR1.BLUE, Driver1.blue-pin
  N11: Driver1.IN1, U1.D25
  N12: Driver1.IN2, U1.D26
  N13: Driver1.IN3, U1.D27
  N14: Driver1.IN4, U1.D14
  GND: Driver1.GND, Driver2.GND, VCC1.-, R3.Pin_1, R4.Pin_0, R5.Pin_1, R6.Pin_0, U1.GND, R7.Pin_0, R8.Pin_0, R9.Pin_0
  N15: Driver1.Vmotor, Driver2.Vmotor, VCC1.+, R2.pin_0, R1.pin_0
  N16: Driver2.IN1, U1.D23
  N17: Driver2.IN2, U1.D22
  N18: Driver2.IN3, U1.D21
  N19: Driver2.IN4, U1.D19
  N20: R2.pin_1, R3.Pin_0, U1.VN
  N21: R4.Pin_1, R1.pin_1, U1.VP
  N22: LED1.anode, U1.D32
  N23: LED2.anode, U1.D33
  N24: U1.D4, LED5.anode
  N25: U1.D5, LED3.anode
  N26: U1.D18, LED4.anode

custom parts:
  28BYJ-48 Driver Module: ULN2003 Driver Module for the 28BYJ-48 Unipolar Stepper Motor LED A - Blue wire - Bottom coil left LED B - Pink wire - Top coil left LED C - Yellow wire - Bottom coil right LED D - Orange wire - Top coil right Common rail - red Connector pins: blue - pink - yellow - orange - red Control pins - IN1 to IN4 Power pins - GND & Vmotor (5-12V) On/Off jumper (if removed, power to motor is cut).
  LuaNode32 / ESP32: New Image for LuaNode32 DOIT ESP32 DEVKIT V1. Base parts from LuaNode32 / ESP32 ESP32 based LuaNode32 by G.Noorlander DOIT Esp32 DevKit v1 (30 pins long, 11 pins width) by Werner Rothschopf (modified by vanepp Dec 2018)
